# Fritzing sketch ultrasonic (saved by Fritzing 0.8.7b)

parts:
  module1 = I2C LCD1602
  元件1 = SunFounder Uno R3
  module2 = Ultrasonic-HC-SRO4

nets:
  N1: module1.SCL, 元件1.A5/SCL
  N2: module1.SDA, 元件1.A4/SDA
  VCC: module1.VCC, 元件1.5V, module2.VCC
  GND: module1.GND, 元件1.GND, module2.GND
  N3: 元件1.D2, module2.TRIG
  N4: 元件1.D3_PWM, module2.ECHO

notes:
  Ultrasonic sensor

custom parts:
  I2C LCD1602: I2C LCD1602 module of SunFounder Sensor Kit
  SunFounder Uno R3: The Arduino Uno is a microcontroller board based on the ATmega328 (datasheet). It has 14 digital input/output pins (of which 6 can be used as PWM outputs), 6 analog inputs, a 16 MHz ceramic resonator, a USB connection, a power jack, an ICSP header, and a reset button. It contains everything needed to support the microcontroller; simply connect it to a computer with a USB cable or power it with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
  Ultrasonic-HC-SRO4: The ultrasonic sensor uses sound to accurately detect objects and measure distances. It sends out ultrasonic waves and converts them into electronic signals
