# Fritzing sketch BMP280_SPI (saved by Fritzing 0.8.7b)
breadboards: 1

parts:
  U1 = BMP280 Module [package="DIP7 [THT]"]
  元件1 = SunFounder Uno R3

nets:
  VCC: U1.VCC, 元件1.5V
  GND: U1.GND, 元件1.GND
  N1: U1.SCK, 元件1.D13/SCK
  N2: U1.SDO, 元件1.ICSP_MISO, 元件1.D12/MISO
  N3: U1.SDI, 元件1.ICSP_MOSI, 元件1.D11_PWM/MOSI
  N4: U1.CS, 元件1.D10_PWM/SS

custom parts:
  BMP280 Module: The BMP280 is an absolute barometric pressure sensor especially designed for mobile applications. The sensor module is housed in an extremely compact 8-pin metal-lid LGA package with a footprint of only 2.0 × 2.5 mm2 and 0.95 mm package height. Its small dimensions and its low power consumption of 2.7 µA @1Hz allow the implementation in battery driven devices such as mobile phones, GPS modules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
  SunFounder Uno R3: The Arduino Uno is a microcontroller board based on the ATmega328 (datasheet). It has 14 digital input/output pins (of which 6 can be used as PWM outputs), 6 analog inputs, a 16 MHz ceramic resonator, a USB connection, a power jack, an ICSP header, and a reset button. It contains everything needed to support the microcontroller; simply connect it to a computer with a USB cable or power it with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
